// Digital circuit 74HC4040.dig as structural Verilog
module _74HC4040 (
  input  nCKin,
  input  CLR,
  input  VCC,
  input  GND,
  output QG,
  output QH,
  output QI,
  output QJ,
  output QD,
  output QE,
  output QF,
  output QC,
  output QA,
  output QB,
  output QK,
  output QL
);

  wire d_ff_as_1_nq, d_ff_as_2_nq, d_ff_as_3_nq, d_ff_as_4_nq, d_ff_as_5_nq, d_ff_as_6_nq, d_ff_as_7_nq,
       d_ff_as_8_nq, d_ff_as_9_nq, d_ff_as_10_nq, d_ff_as_11_nq, d_ff_as_12_nq, not_1_out, not_2_out,
       not_3_out, not_4_out, or_1_out;

  PowerSupply powersupply_1 (.VDD(VCC), .GND(GND));
  not not_1 (not_1_out, CLR);
  or or_1 (or_1_out, ~nCKin, ~not_1_out);  // Or
  not not_2 (not_2_out, not_1_out);
  not not_3 (not_3_out, or_1_out);
  not not_4 (not_4_out, not_3_out);
  D_FF_AS d_ff_as_1 (.Set(1'b0), .D(d_ff_as_1_nq), .C(not_4_out), .Clr(not_2_out), .nQ(d_ff_as_1_nq));  // open: Q
  not not_5 (QA, d_ff_as_1_nq);
  D_FF_AS d_ff_as_2 (.Set(1'b0), .D(d_ff_as_2_nq), .C(d_ff_as_1_nq), .Clr(not_2_out), .nQ(d_ff_as_2_nq));  // open: Q
  not not_6 (QB, d_ff_as_2_nq);
  D_FF_AS d_ff_as_3 (.Set(1'b0), .D(d_ff_as_3_nq), .C(d_ff_as_2_nq), .Clr(not_2_out), .nQ(d_ff_as_3_nq));  // open: Q
  not not_7 (QC, d_ff_as_3_nq);
  D_FF_AS d_ff_as_4 (.Set(1'b0), .D(d_ff_as_4_nq), .C(d_ff_as_3_nq), .Clr(not_2_out), .nQ(d_ff_as_4_nq));  // open: Q
  not not_8 (QD, d_ff_as_4_nq);
  D_FF_AS d_ff_as_5 (.Set(1'b0), .D(d_ff_as_5_nq), .C(d_ff_as_4_nq), .Clr(not_2_out), .nQ(d_ff_as_5_nq));  // open: Q
  not not_9 (QE, d_ff_as_5_nq);
  D_FF_AS d_ff_as_6 (.Set(1'b0), .D(d_ff_as_6_nq), .C(d_ff_as_5_nq), .Clr(not_2_out), .nQ(d_ff_as_6_nq));  // open: Q
  not not_10 (QF, d_ff_as_6_nq);
  D_FF_AS d_ff_as_7 (.Set(1'b0), .D(d_ff_as_7_nq), .C(d_ff_as_6_nq), .Clr(not_2_out), .nQ(d_ff_as_7_nq));  // open: Q
  not not_11 (QG, d_ff_as_7_nq);
  D_FF_AS d_ff_as_8 (.Set(1'b0), .D(d_ff_as_8_nq), .C(d_ff_as_7_nq), .Clr(not_2_out), .nQ(d_ff_as_8_nq));  // open: Q
  not not_12 (QH, d_ff_as_8_nq);
  D_FF_AS d_ff_as_9 (.Set(1'b0), .D(d_ff_as_9_nq), .C(d_ff_as_8_nq), .Clr(not_2_out), .nQ(d_ff_as_9_nq));  // open: Q
  not not_13 (QI, d_ff_as_9_nq);
  D_FF_AS d_ff_as_10 (.Set(1'b0), .D(d_ff_as_10_nq), .C(d_ff_as_9_nq), .Clr(not_2_out), .nQ(d_ff_as_10_nq));  // open: Q
  not not_14 (QJ, d_ff_as_10_nq);
  D_FF_AS d_ff_as_11 (
    .Set(1'b0), .D(d_ff_as_11_nq), .C(d_ff_as_10_nq), .Clr(not_2_out), .nQ(d_ff_as_11_nq));  // open: Q
  not not_15 (QK, d_ff_as_11_nq);
  D_FF_AS d_ff_as_12 (
    .Set(1'b0), .D(d_ff_as_12_nq), .C(d_ff_as_11_nq), .Clr(not_2_out), .nQ(d_ff_as_12_nq));  // open: Q
  not not_16 (QL, d_ff_as_12_nq);

  // Notes on the sheet:
  //   nCKin: pin 10
  //   CLR: pin 11
  //   QG: pin 4
  //   QH: pin 13
  //   QI: pin 12
  //   QJ: pin 14
  //   QD: pin 5
  //   QE: pin 3
  //   QF: pin 2
  //   VCC: pin 16, default 1
  //   GND: pin 8
  //   QC: pin 6
  //   QA: pin 9
  //   QB: pin 7
  //   QK: pin 15
  //   QL: pin 1
endmodule
