// Digital circuit Mini_MITE_1.dig as structural Verilog
module Mini_MITE_1 (
  input  clk,
  output GCLK,
  output nCE,
  output Bout
);

  wire button_1_out, button_2_out, button_3_out, button_4_out, button_5_out, button_6_out, button_7_out,
       button_8_out, D1, D2, D3, D4, D5, D6, D7, d_ff_1_nq, d_ff_2_nq, d_ff_3_nq, d_ff_4_nq, d_ff_5_nq,
       d_ff_6_nq, GATE, IC16_2_nq, IC16_nq, monoflop_1_nq, nand_3_out, nLOAD, not_1_out, not_2_out, nRESET,
       STEP_out, T0, T1, T2, T3, T4, T5, T6, T7, T8, T9;
  wire [3:0] D0, MISO_H, MISO_L;

  _744017 U1 (
    .pin1(T5), .pin2(T1), .pin3(T0), .pin4(T2), .pin5(T6), .pin6(T7), .pin7(T3), .pin8(1'b0), .pin9(T8),
    .pin10(T4), .pin11(T9), .pin13(1'b0), .pin14(clk), .pin15(nCE), .pin16(1'b1));  // open: pin12
  Button STEP (.out(STEP_out));
  Reset reset_1 (.out(nRESET));
  Monoflop monoflop_1 (.C(STEP_out), .R(1'b0), .nQ(monoflop_1_nq));  // open: Q
  not not_1 (not_1_out, T1);
  not not_2 (not_2_out, T9);
  not not_3 (nLOAD, T0);
  _74165 U2 (
    .pin1(nLOAD), .pin2(GCLK), .pin3(D3), .pin4(D2), .pin5(D1), .pin6(D0[0]), .pin8(1'b0), .pin9(Bout),
    .pin10(1'b0), .pin11(D7), .pin12(D6), .pin13(D5), .pin14(D4), .pin15(1'b0), .pin16(1'b1));  // open: pin7
  nand nand_1 (GATE, not_1_out, monoflop_1_nq, nCE);
  nand nand_2 (nCE, GATE, not_2_out);
  nand nand_3 (nand_3_out, GATE, clk);
  not not_4 (GCLK, nand_3_out);
  LED led_1 (.in(D7));
  D_FF IC16 (.D(IC16_nq), .C(button_1_out), .Q(D7), .nQ(IC16_nq));
  LED led_2 (.in(D6));
  D_FF d_ff_1 (.D(d_ff_1_nq), .C(button_2_out), .Q(D6), .nQ(d_ff_1_nq));
  Button button_1 (.out(button_1_out));
  LED led_3 (.in(D5));
  D_FF d_ff_2 (.D(d_ff_2_nq), .C(button_3_out), .Q(D5), .nQ(d_ff_2_nq));
  Button button_2 (.out(button_2_out));
  _74595 U3 (
    .pin1(MISO_H[2]), .pin2(MISO_H[1]), .pin3(MISO_H[0]), .pin4(MISO_L[3]), .pin5(MISO_L[2]),
    .pin6(MISO_L[1]), .pin7(MISO_L[0]), .pin8(1'b0), .pin10(nRESET), .pin11(GCLK), .pin12(nCE), .pin13(1'b0),
    .pin14(Bout), .pin15(MISO_H[3]), .pin16(1'b1));  // open: pin9
  LED led_4 (.in(D4));
  D_FF d_ff_3 (.D(d_ff_3_nq), .C(button_4_out), .Q(D4), .nQ(d_ff_3_nq));
  Button button_3 (.out(button_3_out));
  LED led_5 (.in(D3));
  D_FF d_ff_4 (.D(d_ff_4_nq), .C(button_5_out), .Q(D3), .nQ(d_ff_4_nq));
  Button button_4 (.out(button_4_out));
  LED led_6 (.in(D2));
  D_FF d_ff_5 (.D(d_ff_5_nq), .C(button_6_out), .Q(D2), .nQ(d_ff_5_nq));
  Button button_5 (.out(button_5_out));
  LED led_7 (.in(D1));
  D_FF d_ff_6 (.D(d_ff_6_nq), .C(button_7_out), .Q(D1), .nQ(d_ff_6_nq));
  Button button_6 (.out(button_6_out));
  LED led_8 (.in(D0[0]));
  D_FF IC16_2 (.D(IC16_2_nq), .C(button_8_out), .Q(D0[0]), .nQ(IC16_2_nq));
  Button button_7 (.out(button_7_out));
  Seven_Seg_Hex seven_seg_hex_1 (.d({D7, D6, D5, D4}), .dp(1'b0));
  Button button_8 (.out(button_8_out));
  Seven_Seg_Hex seven_seg_hex_2 (.d(D0), .dp(1'b0));
  Seven_Seg_Hex seven_seg_hex_3 (.d(MISO_H), .dp(1'b0));
  Seven_Seg_Hex seven_seg_hex_4 (.d(MISO_L), .dp(1'b0));
  // Pins of 1 and 4 bits meet at D0

  // Other names for the same wires on the sheet: RD0 = MISO_L[0]; RD1 = MISO_L[1]; RD2 = MISO_L[2]; RD3 = MISO_L[3];
  //   RD4 = MISO_H[0]; RD5 = MISO_H[1]; RD6 = MISO_H[2]; RD7 = MISO_H[3]

  // Notes on the sheet:
  //   clk: Hz: 2147483647
  //   Mini-MITE
  //   8-bit OUTPUT REGISTER
  //   8-bit INPUT REGISTER
  //   Data Input
  //   MOSI
  //   MISO
endmodule
