// Digital circuit Seq_01.dig as structural Verilog
module Seq_01 (
  input  clk,
  input  in_2,
  input  Jump_Inc,
  output MOSI,
  output SCLK,
  output nSS,
  output RCLK,
  output nLOADB,
  output GCLK
);

  wire button_1_out, D0, D1, D2, D3, D4, D5, D6, D7, LD, monoflop_1_q, nand_3_out, nand_4_out, nand_5_out,
       nand_7_out, nand_8_out, nand_10_out, nand_11_out, nand_12_out, nand_13_out, not_1_out, nRESET, nRST,
       nT1, nT18, PC0, PC1, PC2, PC3, PC4, PC5, PC6, PC7, PC8, PC9, PC10, PC11, PC12, PC13, PC14, PC15,
       PC_CARRYIN, PC_CARRYOUT, PC_DATA_IN, PCout, RCO, RST, RUN, T1, T17, T18, U4_pin9;
  wire [2:0] U2_pin12;
  wire [3:0] MISO_H, MISO_L;

  // _28c512 U3: pin names not known; wires that end beside it: PC15, PC12, PC7, PC6, PC5, PC4, PC3, PC2, PC1, PC0, D0, D1, D2, 1'b0, 1'b1, 1'b1, PC14, PC13, PC8, PC9, PC11, 1'b0, PC10
  Reset reset_1 (.out(nRESET));
  Multiplexer multiplexer_1 (.sel(in_2), .in_0(T18), .in_1(monoflop_1_q), .out(RUN));
  Monoflop monoflop_1 (.C(button_1_out), .R(1'b0), .Q(monoflop_1_q));  // open: nQ
  Button button_1 (.out(button_1_out));
  nand nand_1 (RST, nT1, nRST);
  nand nand_2 (nRST, RST, RCLK);
  nand nand_3 (nand_3_out, clk, clk);
  _74165 U6 (
    .pin1(nLOADB), .pin2(GCLK), .pin3(D3), .pin4(D2), .pin5(D1), .pin6(D0), .pin8(1'b0), .pin9(MOSI),
    .pin10(1'b0), .pin11(D7), .pin12(D6), .pin13(D5), .pin14(D4), .pin15(1'b0), .pin16(1'b1));  // open: pin7
  nand nand_4 (nand_4_out, PCout, PC_CARRYIN);
  nand nand_5 (nand_5_out, PCout, PC_CARRYIN);
  nand nand_6 (GCLK, RST, nand_3_out);
  nand nand_7 (nand_7_out, PCout, nand_4_out);
  nand nand_8 (nand_8_out, nand_4_out, PC_CARRYIN);
  nand nand_9 (PC_CARRYOUT, nand_5_out, nand_5_out);
  _74161 U2 (
    .pin1(RST), .pin2(clk), .pin3(1'b0), .pin4(1'b0), .pin5(1'b0), .pin6(1'b0), .pin7(1'b1), .pin8(1'b0),
    .pin9(1'b1), .pin10(1'b1), .pin11(nSS), .pin12(U2_pin12[2]), .pin13(U2_pin12[1]), .pin14(U2_pin12[0]),
    .pin15(RCO), .pin16(1'b1));
  nand nand_10 (nand_10_out, nand_7_out, nand_8_out);
  nand nand_11 (nand_11_out, Jump_Inc, Jump_Inc);
  nand nand_12 (nand_12_out, MOSI, nand_11_out);
  nand nand_13 (nand_13_out, Jump_Inc, nand_10_out);
  Seven_Seg_Hex seven_seg_hex_1 (.d({nSS, U2_pin12}), .dp(1'b0));
  _74595 U7 (
    .pin1(MISO_H[2]), .pin2(MISO_H[1]), .pin3(MISO_H[0]), .pin4(MISO_L[3]), .pin5(MISO_L[2]),
    .pin6(MISO_L[1]), .pin7(MISO_L[0]), .pin8(1'b0), .pin10(nRESET), .pin11(SCLK), .pin12(RCLK),
    .pin13(1'b0), .pin14(MOSI), .pin15(MISO_H[3]), .pin16(1'b1));  // open: pin9
  not not_1 (not_1_out, nSS);
  nand nand_14 (PC_DATA_IN, nand_12_out, nand_13_out);
  nand nand_15 (SCLK, GCLK, not_1_out);
  Seven_Seg_Hex seven_seg_hex_2 (.d({PC15, PC14, PC13, PC12}), .dp(1'b0));
  _7474 U9 (
    .pin1(1'b1), .pin2(1'b1), .pin3(1'b1), .pin4(1'b1), .pin7(1'b0), .pin9(PC_CARRYIN), .pin10(nLOADB),
    .pin11(GCLK), .pin12(PC_CARRYOUT), .pin13(1'b1), .pin14(1'b1));  // open: pin5, pin6, pin8
  _74175 U10 (
    .pin1(nRESET), .pin2(T17), .pin3(RCLK), .pin4(RCO), .pin5(T17), .pin6(nT18), .pin7(T18), .pin8(1'b0),
    .pin9(clk), .pin10(LD), .pin11(nLOADB), .pin12(RUN), .pin13(LD), .pin14(nT1), .pin15(T1), .pin16(1'b1));
  Seven_Seg_Hex seven_seg_hex_3 (.d({PC11, PC10, PC9, PC8}), .dp(1'b0));
  Seven_Seg_Hex seven_seg_hex_4 (.d({PC7, PC6, PC5, PC4}), .dp(1'b0));
  Seven_Seg_Hex seven_seg_hex_5 (.d({PC3, PC2, PC1, PC0}), .dp(1'b0));
  _74595 U4 (
    .pin1(PC14), .pin2(PC13), .pin3(PC12), .pin4(PC11), .pin5(PC10), .pin6(PC9), .pin7(PC8), .pin8(1'b0),
    .pin9(U4_pin9), .pin10(nRESET), .pin11(GCLK), .pin12(RCLK), .pin13(1'b0), .pin14(PC_DATA_IN),
    .pin15(PC15), .pin16(1'b1));
  _74595 U5 (
    .pin1(PC6), .pin2(PC5), .pin3(PC4), .pin4(PC3), .pin5(PC2), .pin6(PC1), .pin7(PC0), .pin8(1'b0),
    .pin9(PCout), .pin10(nRESET), .pin11(GCLK), .pin12(RCLK), .pin13(1'b0), .pin14(U4_pin9), .pin15(PC7),
    .pin16(1'b1));
  Seven_Seg_Hex seven_seg_hex_6 (.d({D7, D6, D5, D4}), .dp(1'b0));
  Seven_Seg_Hex seven_seg_hex_7 (.d({D3, D2, D1, D0}), .dp(1'b0));
  Seven_Seg_Hex seven_seg_hex_8 (.d(MISO_H), .dp(1'b0));
  Seven_Seg_Hex seven_seg_hex_9 (.d(MISO_L), .dp(1'b0));

  // Other names for the same wires on the sheet: IR0 = D0; IR1 = D1; IR2 = D2; IR3 = D3; IR4 = D4; IR5 = D5; IR6 = D6;
  //   IR7 = D7; MISO = MOSI; nT0 = nLOADB; nT17 = RCLK; PC_CLK = GCLK; RD0 = MISO_L[0]; RD1 = MISO_L[1];
  //   RD2 = MISO_L[2]; RD3 = MISO_L[3]; RD4 = MISO_H[0]; RD5 = MISO_H[1]; RD6 = MISO_H[2]; RD7 = MISO_H[3]; T0 = LD

  // Notes on the sheet:
  //   clk: Hz: 4
  //   in_2: default 1
  //   Jump_Inc: default 1
  //   SPI Controller 01
  //   ROM
  //   STEP/RUN
  //   CLOCK SEQUENCER
  //   REGISTERS
  //   PC Half-Adder
  //   U1
  //   8-bit B-REGISTER
  //   8-bit INPUT REGISTER
  //   # Clock
  //   U11
  //   PC ADDRESS
  //   SEQUENCER FFs
  //   PC Carry FF
  //   PC
  //   ROM DATA
  //   MISO
endmodule
