// Digital circuit Seq_01G_with_registers_01.dig as structural Verilog
module Seq_01G_with_registers_01 (
  input  clk,
  input  Inc_nJp,
  input  Dec_nInc,
  input  in_11,
  input  in_12,
  input  in_13,
  input  in_14,
  input  in_15,
  input  in_16,
  input  in_17,
  input  REGWR,
  output MOSI,
  output RCLK,
  output nLOADB,
  output GCLK,
  output nSS,
  output SCLK,
  output MISO
);

  wire _0Q0, _0Q1, _0Q2, _0Q3, _0Q4, _0Q5, _0Q6, _0Q7, _0Q8, _0Q9, _0Q10, _0Q11, _0Q12, _0Q13, _0Q14, _0Q15,
       _74125_1_pin3, _74164_2_pin13, _74164_3_pin13, _74164_4_pin13, _74164_5_pin13, _74164_6_pin13,
       _74164_7_pin13, _74164_8_pin13, button_1_out, D0, D1, D2, D3, D4, D5, D6, D7, eq_42, LD, nand_5_out,
       nand_6_out, nand_7_out, nand_9_out, nand_10_out, nand_11_out, nand_13_out, nand_14_out, nand_15_out,
       nand_16_out, nand_17_out, nand_18_out, nand_19_out, nand_20_out, nand_21_out, nand_22_out,
       nand_23_out, nand_24_out, nand_25_out, nand_26_out, nand_27_out, nand_28_out, nand_29_out,
       nand_30_out, nand_31_out, nand_32_out, nand_33_out, nand_34_out, nand_35_out, nand_36_out, nCLK,
       not_1_out, nRESET, nRST, nT1, nT18, PC0, PC1, PC2, PC3, PC4, PC5, PC6, PC7, PC8, PC9, PC10, PC11,
       PC12, PC13, PC14, PC15, PC_CIN, PC_COUT, PC_Din, PC_Dout, Q_D, RCO, RST, RUN, S_IN0, S_IN1, S_IN2,
       S_IN3, S_IN4, S_IN5, S_IN6, S_IN7, SER, SIN0, SIN1, SIN2, SIN3, SIN4, SIN5, SIN6, SIN7, SOUT1, SOUT2,
       SOUT3, SOUT4, SOUT5, SOUT6, SOUT7, Sum, T1, T17, T18, TogglenSS, U9_pin2, W0, W1, W2, W3, W4, W5, W6,
       W7, xor_1_out, xor_3_out;
  wire [2:0] U2_pin12;
  wire [3:0] _42H, _42L, MISO_H, MISO_L;

  Seven_Seg_Hex seven_seg_hex_1 (.d({PC15, PC14, PC13, PC12}), .dp(1'b0));
  // _28c512 U3: pin names not known; wires that end beside it: PC15, PC12, PC7, PC6, PC5, PC4, PC3, PC2, PC1, PC0, D0, D1, D2, 1'b0, 1'b1, 1'b1, PC14, PC13, PC8, PC9, PC11, 1'b0, PC10
  Reset reset_1 (.out(nRESET));
  Monoflop monoflop_1 (.C(button_1_out), .R(1'b0), .Q(RUN));  // open: nQ
  Button button_1 (.out(button_1_out));
  Seven_Seg_Hex seven_seg_hex_2 (.d({PC11, PC10, PC9, PC8}), .dp(1'b0));
  Seven_Seg_Hex seven_seg_hex_3 (.d({PC7, PC6, PC5, PC4}), .dp(1'b0));
  Seven_Seg_Hex seven_seg_hex_4 (.d({PC3, PC2, PC1, PC0}), .dp(1'b0));
  Seven_Seg_Hex seven_seg_hex_5 (.d({D7, D6, D5, D4}), .dp(1'b0));
  Seven_Seg_Hex seven_seg_hex_6 (.d({D3, D2, D1, D0}), .dp(1'b0));
  Seven_Seg_Hex seven_seg_hex_7 (.d(MISO_H), .dp(1'b0));
  nand nand_1 (RST, nT1, nRST);
  nand nand_2 (nRST, RST, RCLK);
  nand nand_3 (GCLK, nCLK, RST);
  nand nand_4 (nCLK, clk, clk);
  _74165 U6 (
    .pin1(nLOADB), .pin2(GCLK), .pin3(D3), .pin4(D2), .pin5(D1), .pin6(D0), .pin8(1'b0), .pin9(MOSI),
    .pin10(1'b0), .pin11(D7), .pin12(D6), .pin13(D5), .pin14(D4), .pin15(1'b0), .pin16(1'b1));  // open: pin7
  _74595 U7 (
    .pin1(MISO_H[2]), .pin2(MISO_H[1]), .pin3(MISO_H[0]), .pin4(MISO_L[3]), .pin5(MISO_L[2]),
    .pin6(MISO_L[1]), .pin7(MISO_L[0]), .pin8(1'b0), .pin10(nRESET), .pin11(SCLK), .pin12(RCLK),
    .pin13(1'b0), .pin14(MISO), .pin15(MISO_H[3]), .pin16(1'b1));  // open: pin9
  Seven_Seg_Hex seven_seg_hex_8 (.d(MISO_L), .dp(1'b0));
  Seven_Seg_Hex seven_seg_hex_9 (.d(_42H), .dp(1'b0));
  Seven_Seg_Hex seven_seg_hex_10 (.d(_42L), .dp(1'b0));
  _74161 U2 (
    .pin1(RST), .pin2(clk), .pin3(1'b0), .pin4(1'b0), .pin5(1'b0), .pin6(1'b0), .pin7(1'b1), .pin8(1'b0),
    .pin9(1'b1), .pin10(1'b1), .pin11(Q_D), .pin12(U2_pin12[2]), .pin13(U2_pin12[1]), .pin14(U2_pin12[0]),
    .pin15(RCO), .pin16(1'b1));
  xor xor_1 (xor_1_out, MOSI, PC_Din);
  _74595 U4 (
    .pin1(PC14), .pin2(PC13), .pin3(PC12), .pin4(PC11), .pin5(PC10), .pin6(PC9), .pin7(PC8), .pin8(1'b0),
    .pin9(SER), .pin10(nRESET), .pin11(GCLK), .pin12(RCLK), .pin13(1'b0), .pin14(PC_Din), .pin15(PC15),
    .pin16(1'b1));
  Seven_Seg_Hex seven_seg_hex_11 (.d({Q_D, U2_pin12}), .dp(1'b0));
  _74595 U13 (
    .pin1(_42H[2]), .pin2(_42H[1]), .pin3(_42H[0]), .pin4(_42L[3]), .pin5(_42L[2]), .pin6(_42L[1]),
    .pin7(_42L[0]), .pin8(1'b0), .pin10(nRESET), .pin11(SCLK), .pin12(RCLK), .pin13(1'b0), .pin14(xor_1_out),
    .pin15(_42H[3]), .pin16(1'b1));  // open: pin9
  nand nand_5 (nand_5_out, _42L[1], _42H[2]);
  xor xor_2 (TogglenSS, 1'b1, eq_42);
  DiodeForward diodeforward_1 (.in(_42L[0]), .out(eq_42));
  DiodeForward diodeforward_2 (.in(_42H[3]), .out(eq_42));
  DiodeForward diodeforward_3 (.in(_42H[1]), .out(eq_42));
  DiodeForward diodeforward_4 (.in(_42H[0]), .out(eq_42));
  DiodeForward diodeforward_5 (.in(_42L[3]), .out(eq_42));
  DiodeForward diodeforward_6 (.in(_42L[2]), .out(eq_42));
  DiodeForward diodeforward_7 (.in(nand_5_out), .out(eq_42));
  nand nand_6 (nand_6_out, Q_D, Q_D);
  nand nand_7 (nand_7_out, Inc_nJp, Inc_nJp);
  xor xor_3 (xor_3_out, Dec_nInc, PC_Dout);
  PullDown pulldown_1 (.out(eq_42));
  _74595 U5 (
    .pin1(PC6), .pin2(PC5), .pin3(PC4), .pin4(PC3), .pin5(PC2), .pin6(PC1), .pin7(PC0), .pin8(1'b0),
    .pin9(PC_Dout), .pin10(nRESET), .pin11(GCLK), .pin12(RCLK), .pin13(1'b0), .pin14(SER), .pin15(PC7),
    .pin16(1'b1));
  nand nand_8 (SCLK, nand_6_out, GCLK);
  nand nand_9 (nand_9_out, MOSI, nand_7_out);
  nand nand_10 (nand_10_out, Inc_nJp, Sum);
  nand nand_11 (nand_11_out, xor_3_out, PC_CIN);
  xor xor_4 (Sum, PC_CIN, PC_Dout);
  nand nand_12 (PC_Din, nand_9_out, nand_10_out);
  xor xor_5 (PC_COUT, 1'b1, nand_11_out);
  _7474 U9 (
    .pin1(1'b1), .pin2(U9_pin2), .pin3(TogglenSS), .pin4(nRESET), .pin5(nSS), .pin6(U9_pin2), .pin7(1'b0),
    .pin9(PC_CIN), .pin10(nLOADB), .pin11(GCLK), .pin12(PC_COUT), .pin13(1'b1), .pin14(1'b1));  // open: pin8
  LED led_1 (.in(nSS));
  _74175 U10 (
    .pin1(nRESET), .pin2(T17), .pin3(RCLK), .pin4(RCO), .pin5(T17), .pin6(nT18), .pin7(T18), .pin8(1'b0),
    .pin9(clk), .pin10(LD), .pin11(nLOADB), .pin12(RUN), .pin13(LD), .pin14(nT1), .pin15(T1), .pin16(1'b1));
  _74138 _74138_1 (
    .pin1(in_14), .pin2(in_15), .pin3(in_16), .pin4(1'b0), .pin5(1'b0), .pin6(REGWR), .pin7(W7), .pin8(1'b0),
    .pin9(W6), .pin10(W5), .pin11(W4), .pin12(W3), .pin13(W2), .pin14(W1), .pin15(W0), .pin16(1'b1));
  _74138 _74138_2 (
    .pin1(in_14), .pin2(in_15), .pin3(in_16), .pin4(MOSI), .pin5(MOSI), .pin6(1'b1), .pin7(S_IN7),
    .pin8(1'b0), .pin9(S_IN6), .pin10(S_IN5), .pin11(S_IN4), .pin12(S_IN3), .pin13(S_IN2), .pin14(S_IN1),
    .pin15(S_IN0), .pin16(1'b1));
  _74151 _74151_1 (
    .pin1(SOUT3), .pin2(SOUT2), .pin3(SOUT1), .pin4(_0Q0), .pin5(MISO), .pin7(in_17), .pin8(1'b0),
    .pin9(in_16), .pin10(in_15), .pin11(in_14), .pin12(SOUT7), .pin13(SOUT6), .pin14(SOUT5), .pin15(SOUT4),
    .pin16(1'b1));  // open: pin6
  nand nand_13 (nand_13_out, W0, W0);
  nand nand_14 (nand_14_out, W1, W1);
  nand nand_15 (nand_15_out, W2, W2);
  nand nand_16 (nand_16_out, W3, W3);
  nand nand_17 (nand_17_out, W4, W4);
  nand nand_18 (nand_18_out, W5, W5);
  nand nand_19 (nand_19_out, W6, W6);
  nand nand_20 (nand_20_out, W7, W7);
  nand nand_21 (nand_21_out, _0Q0, W0);
  nand nand_22 (nand_22_out, nand_13_out, S_IN0);
  nand nand_23 (nand_23_out, SOUT1, W1);
  nand nand_24 (nand_24_out, nand_14_out, S_IN1);
  nand nand_25 (nand_25_out, SOUT2, W2);
  nand nand_26 (nand_26_out, nand_15_out, S_IN2);
  nand nand_27 (nand_27_out, SOUT3, W3);
  nand nand_28 (nand_28_out, nand_16_out, S_IN3);
  nand nand_29 (nand_29_out, SOUT4, W4);
  nand nand_30 (nand_30_out, nand_17_out, S_IN4);
  nand nand_31 (nand_31_out, SOUT5, W5);
  nand nand_32 (nand_32_out, nand_18_out, S_IN5);
  nand nand_33 (nand_33_out, SOUT6, W6);
  nand nand_34 (nand_34_out, nand_19_out, S_IN6);
  nand nand_35 (nand_35_out, SOUT7, W7);
  nand nand_36 (nand_36_out, nand_20_out, S_IN7);
  nand nand_37 (SIN0, nand_21_out, nand_22_out);
  nand nand_38 (SIN1, nand_23_out, nand_24_out);
  nand nand_39 (SIN2, nand_25_out, nand_26_out);
  nand nand_40 (SIN3, nand_27_out, nand_28_out);
  nand nand_41 (SIN4, nand_29_out, nand_30_out);
  nand nand_42 (SIN5, nand_31_out, nand_32_out);
  nand nand_43 (SIN6, nand_33_out, nand_34_out);
  nand nand_44 (SIN7, nand_35_out, nand_36_out);
  _74164 _74164_1 (
    .pin1(1'b1), .pin2(SIN0), .pin3(_0Q15), .pin4(_0Q14), .pin5(_0Q13), .pin6(_0Q12), .pin7(1'b0),
    .pin8(SCLK), .pin9(nRESET), .pin10(_0Q11), .pin11(_0Q10), .pin12(_0Q9), .pin13(_0Q8), .pin14(1'b1));
  _74164 _74164_2 (
    .pin1(1'b1), .pin2(SIN1), .pin7(1'b0), .pin8(SCLK), .pin9(nRESET), .pin13(_74164_2_pin13), .pin14(1'b1));  // open: pin3, pin4, pin5, pin6, pin10, pin11, pin12
  _74164 _74164_3 (
    .pin1(1'b1), .pin2(SIN2), .pin7(1'b0), .pin8(SCLK), .pin9(nRESET), .pin13(_74164_3_pin13), .pin14(1'b1));  // open: pin3, pin4, pin5, pin6, pin10, pin11, pin12
  _74164 _74164_4 (
    .pin1(1'b1), .pin2(SIN3), .pin7(1'b0), .pin8(SCLK), .pin9(nRESET), .pin13(_74164_4_pin13), .pin14(1'b1));  // open: pin3, pin4, pin5, pin6, pin10, pin11, pin12
  _74164 _74164_5 (
    .pin1(1'b1), .pin2(SIN4), .pin7(1'b0), .pin8(SCLK), .pin9(nRESET), .pin13(_74164_5_pin13), .pin14(1'b1));  // open: pin3, pin4, pin5, pin6, pin10, pin11, pin12
  _74164 _74164_6 (
    .pin1(1'b1), .pin2(SIN5), .pin7(1'b0), .pin8(SCLK), .pin9(nRESET), .pin13(_74164_6_pin13), .pin14(1'b1));  // open: pin3, pin4, pin5, pin6, pin10, pin11, pin12
  _74164 _74164_7 (
    .pin1(1'b1), .pin2(SIN6), .pin7(1'b0), .pin8(SCLK), .pin9(nRESET), .pin13(_74164_7_pin13), .pin14(1'b1));  // open: pin3, pin4, pin5, pin6, pin10, pin11, pin12
  _74164 _74164_8 (
    .pin1(1'b1), .pin2(SIN7), .pin7(1'b0), .pin8(SCLK), .pin9(nRESET), .pin13(_74164_8_pin13), .pin14(1'b1));  // open: pin3, pin4, pin5, pin6, pin10, pin11, pin12
  Seven_Seg_Hex seven_seg_hex_12 (.d({_0Q15, _0Q14, _0Q13, _0Q12}), .dp(1'b0));
  Seven_Seg_Hex seven_seg_hex_13 (.d({_0Q11, _0Q10, _0Q9, _0Q8}), .dp(1'b0));
  Seven_Seg_Hex seven_seg_hex_14 (.d({_0Q7, _0Q6, _0Q5, _0Q4}), .dp(1'b0));
  _74164 _74164_9 (
    .pin1(1'b1), .pin2(_0Q8), .pin3(_0Q7), .pin4(_0Q6), .pin5(_0Q5), .pin6(_0Q4), .pin7(1'b0), .pin8(SCLK),
    .pin9(nRESET), .pin10(_0Q3), .pin11(_0Q2), .pin12(_0Q1), .pin13(_0Q0), .pin14(1'b1));
  _74164 _74164_10 (
    .pin1(1'b1), .pin2(_74164_2_pin13), .pin7(1'b0), .pin8(SCLK), .pin9(nRESET), .pin13(SOUT1), .pin14(1'b1));  // open: pin3, pin4, pin5, pin6, pin10, pin11, pin12
  _74164 _74164_11 (
    .pin1(1'b1), .pin2(_74164_3_pin13), .pin7(1'b0), .pin8(SCLK), .pin9(nRESET), .pin13(SOUT2), .pin14(1'b1));  // open: pin3, pin4, pin5, pin6, pin10, pin11, pin12
  _74164 _74164_12 (
    .pin1(1'b1), .pin2(_74164_4_pin13), .pin7(1'b0), .pin8(SCLK), .pin9(nRESET), .pin13(SOUT3), .pin14(1'b1));  // open: pin3, pin4, pin5, pin6, pin10, pin11, pin12
  _74164 _74164_13 (
    .pin1(1'b1), .pin2(_74164_5_pin13), .pin7(1'b0), .pin8(SCLK), .pin9(nRESET), .pin13(SOUT4), .pin14(1'b1));  // open: pin3, pin4, pin5, pin6, pin10, pin11, pin12
  _74164 _74164_14 (
    .pin1(1'b1), .pin2(_74164_6_pin13), .pin7(1'b0), .pin8(SCLK), .pin9(nRESET), .pin13(SOUT5), .pin14(1'b1));  // open: pin3, pin4, pin5, pin6, pin10, pin11, pin12
  _74164 _74164_15 (
    .pin1(1'b1), .pin2(_74164_7_pin13), .pin7(1'b0), .pin8(SCLK), .pin9(nRESET), .pin13(SOUT6), .pin14(1'b1));  // open: pin3, pin4, pin5, pin6, pin10, pin11, pin12
  _74164 _74164_16 (
    .pin1(1'b1), .pin2(_74164_8_pin13), .pin7(1'b0), .pin8(SCLK), .pin9(nRESET), .pin13(SOUT7), .pin14(1'b1));  // open: pin3, pin4, pin5, pin6, pin10, pin11, pin12
  Seven_Seg_Hex seven_seg_hex_15 (.d({_0Q3, _0Q2, _0Q1, _0Q0}), .dp(1'b0));
  not not_1 (not_1_out, in_13);
  _74125 _74125_1 (
    .pin1(not_1_out), .pin2(in_11), .pin3(_74125_1_pin3), .pin4(in_13), .pin5(in_12), .pin6(_74125_1_pin3),
    .pin7(1'b0), .pin9(1'b1), .pin10(1'b1), .pin12(1'b1), .pin13(1'b1), .pin14(1'b1));  // open: pin8, pin11

  // Other names for the same wires on the sheet: E0 = in_14; E1 = in_15; E2 = in_16; IR0 = D0; IR1 = D1; IR2 = D2;
  //   IR3 = D3; IR4 = D4; IR5 = D5; IR6 = D6; IR7 = D7; nT0 = nLOADB; nT17 = RCLK; PC_CLK = GCLK; RD0 = MISO_L[0];
  //   RD1 = MISO_L[1]; RD2 = MISO_L[2]; RD3 = MISO_L[3]; RD4 = MISO_H[0]; RD5 = MISO_H[1]; RD6 = MISO_H[2];
  //   RD7 = MISO_H[3]; REG_CLK = SCLK; SOUT0 = _0Q0; T0 = LD

  // Notes on the sheet:
  //   clk: Hz: 16
  //   Inc_nJp: default 1
  //   SPI Controller 01
  //   ROM
  //   STEP/RUN
  //   PC ADDRESS
  //   MOSI
  //   CLOCK SEQUENCER
  //   U1
  //   8-bit OUTPUT REGISTER
  //   8-bit INPUT REGISTER
  //   MISO
  //   XOR Instr
  //   "42"
  //   PC
  //   # Clock
  //   U12B
  //   U11D
  //   U12A
  //   PC Half-Add/Sub
  //   $42 Detect
  //   U11A
  //   U8
  //   D-FFs
  //   U11B
  //   U11C
  //   U12C
  //   PC Carry FF
  //   SEQUENCER FFs
  //   U12D
  //   SERIAL REGISTERS
  //   REGISTER R0
endmodule
