// Digital circuit Seq_10_Controller.dig as structural Verilog
module Seq_10_Controller (
  input  clk,
  input  in_2,
  output Bout,
  output SCLK,
  output nSS,
  output RCLK,
  output nLOADB
);

  wire ALU_CARRY, ALU_SUM, and_1_out, and_3_out, button_1_out, CARRY, Cin, D0, D1, D2, D3, D4, D5, D6, D7,
       diodeforward_3_out, Fout, GCLK, I0, I1, LD, LONGJUMP, monoflop_1_q, nand_8_out, nB, nCLR, nCRES,
       nCSET, nCSup, nJMP, not_1_out, not_2_out, not_3_out, nRESET, nRST, nSETSR, nT18, nY0, nY2, nY3, nY4,
       nY5, nY6, PC0, PC1, PC2, PC3, PC4, PC5, PC6, PC7, PC8, PC9, PC10, PC11, PC12, PC13, PC14, PC15,
       PC_CARRYIN, PC_CARRYOUT, PC_DATA_IN, PC_in, PCout, RCO, RST, RUN, SETC, T17, T18, U4_pin9, U8_pin8,
       U8_pin11, U13_pin14, xor_2_out, ZERO, Zin;
  wire [2:0] U2_pin12;
  wire [3:0] MISO_H, MISO_L;

  Seven_Seg_Hex seven_seg_hex_1 (.d(MISO_H), .dp(1'b0));
  Seven_Seg_Hex seven_seg_hex_2 (.d(MISO_L), .dp(1'b0));
  _74138 U17 (
    .pin1(D4), .pin2(D5), .pin3(D6), .pin4(1'b0), .pin5(1'b0), .pin6(1'b1), .pin7(nJMP), .pin8(1'b0),
    .pin9(nY6), .pin10(nY5), .pin11(nY4), .pin12(nY3), .pin13(nY2), .pin14(I0), .pin15(nY0), .pin16(1'b1));
  Reset reset_1 (.out(nRESET));
  Multiplexer multiplexer_1 (.sel(in_2), .in_0(T18), .in_1(monoflop_1_q), .out(RUN));
  Monoflop monoflop_1 (.C(button_1_out), .R(1'b0), .Q(monoflop_1_q));  // open: nQ
  Button button_1 (.out(button_1_out));
  Seven_Seg_Hex seven_seg_hex_3 (.d({PC15, PC14, PC13, PC12}), .dp(1'b0));
  Seven_Seg_Hex seven_seg_hex_4 (.d({PC11, PC10, PC9, PC8}), .dp(1'b0));
  Seven_Seg_Hex seven_seg_hex_5 (.d({PC7, PC6, PC5, PC4}), .dp(1'b0));
  xor xor_1 (nB, 1'b1, nY5);
  xor xor_2 (xor_2_out, 1'b1, nY0);
  and and_1 (and_1_out, I0, nY2, nY3);
  Seven_Seg_Hex seven_seg_hex_6 (.d({PC3, PC2, PC1, PC0}), .dp(1'b0));
  not not_1 (not_1_out, nJMP);
  nand nand_1 (LONGJUMP, not_1_out, D3);
  Seven_Seg_Hex seven_seg_hex_7 (.d({D7, D6, D5, D4}), .dp(1'b0));
  nand nand_2 (nCSup, LD, nY5);
  nand nand_3 (nCSET, nB, SETC);
  nand nand_4 (I1, I0, nY2);
  nand nand_5 (nCLR, LD, xor_2_out);
  and and_2 (nCRES, 1'b1, and_1_out, nCSup);
  Seven_Seg_Hex seven_seg_hex_8 (.d({D3, D2, D1, D0}), .dp(1'b0));
  nand nand_6 (RST, nSETSR, nRST);
  nand nand_7 (nRST, RST, RCLK);
  nand nand_8 (nand_8_out, clk, clk);
  _74165 U6 (
    .pin1(nLOADB), .pin2(GCLK), .pin3(D3), .pin4(D2), .pin5(D1), .pin6(D0), .pin8(1'b0), .pin9(Bout),
    .pin10(1'b0), .pin11(D7), .pin12(D6), .pin13(D5), .pin14(D4), .pin15(1'b0), .pin16(1'b1));  // open: pin7
  not not_2 (not_2_out, nJMP);
  _74283 U13 (
    .pin1(PC_CARRYOUT), .pin2(1'b0), .pin3(1'b0), .pin4(PC_DATA_IN), .pin5(1'b0), .pin6(PCout),
    .pin7(PC_CARRYIN), .pin8(1'b0), .pin9(ALU_CARRY), .pin10(ALU_SUM), .pin11(Cin), .pin12(Bout),
    .pin14(U13_pin14), .pin15(1'b1), .pin16(1'b1));  // open: pin13
  nand nand_9 (GCLK, RST, nand_8_out);
  _74126 U8 (
    .pin1(nJMP), .pin2(PC_DATA_IN), .pin3(PC_in), .pin4(not_2_out), .pin5(Bout), .pin6(PC_in), .pin7(1'b0),
    .pin8(U8_pin8), .pin9(ALU_CARRY), .pin10(I1), .pin11(U8_pin11), .pin12(ALU_SUM), .pin13(I0), .pin14(1'b1));
  DiodeForward diodeforward_1 (.in(U8_pin11), .out(Fout));
  DiodeForward diodeforward_2 (.in(U8_pin8), .out(Fout));
  xor xor_3 (U13_pin14, Bout, nB);
  PullDown pulldown_1 (.out(Fout));
  _74161 U2 (
    .pin1(RST), .pin2(clk), .pin3(1'b0), .pin4(1'b0), .pin5(1'b0), .pin6(1'b0), .pin7(1'b1), .pin8(1'b0),
    .pin9(1'b1), .pin10(1'b1), .pin11(nSS), .pin12(U2_pin12[2]), .pin13(U2_pin12[1]), .pin14(U2_pin12[0]),
    .pin15(RCO), .pin16(1'b1));
  LED led_1 (.in(ZERO));
  _7474 U9 (
    .pin1(nCRES), .pin2(ALU_CARRY), .pin3(GCLK), .pin4(nCSET), .pin5(Cin), .pin7(1'b0), .pin9(PC_CARRYIN),
    .pin10(nLOADB), .pin11(GCLK), .pin12(PC_CARRYOUT), .pin13(1'b1), .pin14(1'b1));  // open: pin6, pin8
  _7474 U14 (
    .pin1(1'b1), .pin2(Zin), .pin3(clk), .pin4(1'b1), .pin5(ZERO), .pin7(1'b0), .pin9(CARRY), .pin10(1'b1),
    .pin11(clk), .pin12(1'b1), .pin13(1'b1), .pin14(1'b1));  // open: pin6, pin8
  _74595 U7 (
    .pin1(MISO_H[2]), .pin2(MISO_H[1]), .pin3(MISO_H[0]), .pin4(MISO_L[3]), .pin5(MISO_L[2]),
    .pin6(MISO_L[1]), .pin7(MISO_L[0]), .pin8(1'b0), .pin10(nRESET), .pin11(SCLK), .pin12(RCLK),
    .pin13(1'b0), .pin14(Bout), .pin15(MISO_H[3]), .pin16(1'b1));  // open: pin9
  Seven_Seg_Hex seven_seg_hex_9 (.d({nSS, U2_pin12}), .dp(1'b0));
  LED led_2 (.in(CARRY));
  not not_3 (not_3_out, nSS);
  and and_3 (and_3_out, GCLK, not_3_out);
  _74175 U10 (
    .pin1(nRESET), .pin2(T17), .pin3(RCLK), .pin4(RCO), .pin5(T17), .pin6(nT18), .pin7(T18), .pin8(1'b0),
    .pin9(clk), .pin10(LD), .pin11(nLOADB), .pin12(RUN), .pin13(LD), .pin14(nSETSR), .pin15(SETC),
    .pin16(1'b1));
  _74153 U15 (
    .pin1(nJMP), .pin2(MISO_H[3]), .pin3(1'b0), .pin4(D2), .pin5(D1), .pin6(D0), .pin8(1'b0), .pin10(1'b0),
    .pin11(1'b0), .pin12(1'b0), .pin13(1'b0), .pin14(ZERO), .pin15(1'b0), .pin16(1'b1));  // open: pin7, pin9
  not not_4 (SCLK, and_3_out);
  _74595 U4 (
    .pin1(PC14), .pin2(PC13), .pin3(PC12), .pin4(PC11), .pin5(PC10), .pin6(PC9), .pin7(PC8), .pin8(1'b0),
    .pin9(U4_pin9), .pin10(nRESET), .pin11(GCLK), .pin12(RCLK), .pin13(1'b0), .pin14(PC_in), .pin15(PC15),
    .pin16(1'b1));
  _74595 U5 (
    .pin1(PC6), .pin2(PC5), .pin3(PC4), .pin4(PC3), .pin5(PC2), .pin6(PC1), .pin7(PC0), .pin8(1'b0),
    .pin9(PCout), .pin10(nRESET), .pin11(GCLK), .pin12(RCLK), .pin13(1'b0), .pin14(U4_pin9), .pin15(PC7),
    .pin16(1'b1));
  // _28c512 U3: pin names not known; wires that end beside it: PC15, PC12, PC7, PC6, PC5, PC4, PC3, PC2, PC1, PC0, D0, D1, D2, 1'b0, 1'b1, 1'b1, PC14, PC13, PC8, PC9, PC11, 1'b0, PC10
  DiodeForward diodeforward_3 (.in(MISO_H[3]), .out(diodeforward_3_out));
  DiodeForward diodeforward_4 (.in(MISO_H[2]), .out(diodeforward_3_out));
  DiodeForward diodeforward_5 (.in(MISO_H[1]), .out(diodeforward_3_out));
  DiodeForward diodeforward_6 (.in(MISO_H[0]), .out(diodeforward_3_out));
  DiodeForward diodeforward_7 (.in(MISO_L[3]), .out(diodeforward_3_out));
  DiodeForward diodeforward_8 (.in(MISO_L[2]), .out(diodeforward_3_out));
  DiodeForward diodeforward_9 (.in(MISO_L[1]), .out(diodeforward_3_out));
  DiodeForward diodeforward_10 (.in(MISO_L[0]), .out(diodeforward_3_out));
  xor xor_4 (Zin, 1'b1, diodeforward_3_out);
  PullDown pulldown_2 (.out(diodeforward_3_out));

  // Other names for the same wires on the sheet: IR0 = D0; IR1 = D1; IR2 = D2; IR3 = D3; IR4 = D4; IR5 = D5; IR6 = D6;
  //   IR7 = D7; MISO = Bout; nT0 = nLOADB; nT1 = nSETSR; nRESETSR = RCLK; nT17 = RCLK; nY1 = I0; nY7 = nJMP;
  //   PC_CLK = GCLK; RD0 = MISO_L[0]; RD1 = MISO_L[1]; RD2 = MISO_L[2]; RD3 = MISO_L[3]; RD4 = MISO_H[0];
  //   RD5 = MISO_H[1]; RD6 = MISO_H[2]; RD7 = MISO_H[3]; T0 = LD; T1 = SETC

  // Notes on the sheet:
  //   clk: Hz: 8
  //   in_2: default 1
  //   SPI Controller 10
  //   MISO
  //   INSTRUCTION DECODER
  //   STEP/RUN
  //   PC ADDRESS
  //   U12B
  //   U12C
  //   74HC11
  //   U11A
  //   Suppress Carry
  //   ROM DATA
  //   U13
  //   74HC1
  //   U11B
  //   U16
  //   CLOCK SEQUENCER
  //   U1
  //   REGISTERS
  //   ALU
  //   8-bit B-REGISTER
  //   PC / ALU MUX
  //   U12D
  //   Carry FF
  //   ZERO/CARRY FFs
  //   PC Carry FF
  //   # Clock
  //   BRANCH CONDITION
  //   SEQUENCER FFs
  //   PC & ROM
  //   Zero Detect
  //   U12A
endmodule
