// Digital circuit Seq_and_PROM_3.dig as structural Verilog
module Seq_and_PROM_3 (
  input  clk,
  input  Inc_nJp,
  input  Inc_nJump1,
  input  nSEL,
  input  in_10,
  input  in_11,
  input  in_12,
  output MOSI,
  output RCLK,
  output nLOADB,
  output GCLK,
  output nSS,
  output TC,
  output SCLK
);

  wire A0, A1, A2, A3, A4, A5, A6, A7, A8, A9, A10, A11, A12, A13, A14, A15, BUS0, BUS1, BUS2, BUS3, BUS4,
       BUS5, BUS6, BUS7, button_1_out, D0, D1, D2, D3, D4, D5, D6, D7, eq_42, LD, MISO, nand_5_out,
       nand_6_out, nand_8_out, nand_9_out, nand_11_out, nand_12_out, nand_15_out, nand_16_out, nand_17_out,
       nand_18_out, nand_19_out, nand_20_out, nand_21_out, nand_25_out, nCLK, nCLR, nRESET, nRST, nT1, nT18,
       nTC, PC0, PC1, PC2, PC3, PC4, PC5, PC6, PC7, PC8, PC9, PC10, PC11, PC12, PC13, PC14, PC15, PC_CIN,
       PC_COUT, PC_Din, PC_Dout, RCO, RPC_CIN, RPC_COUT, RPC_DIN, RPC_Dout, RST, RUN, SEL, SER, Sum, T1, T17,
       T18, TogglenSS, U9_pin2, U21_pin9, xor_1_out;
  wire [3:0] MISO_H, MISO_L, U2_pin11, U13_pin3, U13_pin7, U29_pin14;

  Seven_Seg_Hex seven_seg_hex_1 (.d({PC15, PC14, PC13, PC12}), .dp(1'b0));
  Seven_Seg_Hex seven_seg_hex_2 (.d({PC11, PC10, PC9, PC8}), .dp(1'b0));
  // _28c512 U3: pin names not known; wires that end beside it: PC15, PC12, PC7, PC6, PC5, PC4, PC3, PC2, PC1, PC0, D0, D1, D2, 1'b0, 1'b1, 1'b1, PC14, PC13, PC8, PC9, PC11, 1'b0, PC10
  Reset reset_1 (.out(nRESET));
  Monoflop monoflop_1 (.C(button_1_out), .R(1'b0), .Q(RUN));  // open: nQ
  Button button_1 (.out(button_1_out));
  Seven_Seg_Hex seven_seg_hex_3 (.d({PC7, PC6, PC5, PC4}), .dp(1'b0));
  Seven_Seg_Hex seven_seg_hex_4 (.d({PC3, PC2, PC1, PC0}), .dp(1'b0));
  Seven_Seg_Hex seven_seg_hex_5 (.d({D7, D6, D5, D4}), .dp(1'b0));
  Seven_Seg_Hex seven_seg_hex_6 (.d({D3, D2, D1, D0}), .dp(1'b0));
  Seven_Seg_Hex seven_seg_hex_7 (.d(MISO_H), .dp(1'b0));
  Seven_Seg_Hex seven_seg_hex_8 (.d(MISO_L), .dp(1'b0));
  nand nand_1 (RST, nT1, nRST);
  nand nand_2 (nRST, RST, RCLK);
  nand nand_3 (GCLK, nCLK, RST);
  nand nand_4 (nCLK, clk, clk);
  _74165 U6 (
    .pin1(nLOADB), .pin2(GCLK), .pin3(D3), .pin4(D2), .pin5(D1), .pin6(D0), .pin8(1'b0), .pin9(MOSI),
    .pin10(1'b0), .pin11(D7), .pin12(D6), .pin13(D5), .pin14(D4), .pin15(1'b0), .pin16(1'b1));  // open: pin7
  _74595 U7 (
    .pin1(MISO_H[2]), .pin2(MISO_H[1]), .pin3(MISO_H[0]), .pin4(MISO_L[3]), .pin5(MISO_L[2]),
    .pin6(MISO_L[1]), .pin7(MISO_L[0]), .pin8(1'b0), .pin10(nRESET), .pin11(SCLK), .pin12(RCLK),
    .pin13(1'b0), .pin14(MISO), .pin15(MISO_H[3]), .pin16(1'b1));  // open: pin9
  Seven_Seg_Hex seven_seg_hex_9 (.d(U13_pin3), .dp(1'b0));
  Seven_Seg_Hex seven_seg_hex_10 (.d(U13_pin7), .dp(1'b0));
  _74161 U2 (
    .pin1(RST), .pin2(clk), .pin3(1'b0), .pin4(1'b0), .pin5(1'b0), .pin6(1'b0), .pin7(1'b1), .pin8(1'b0),
    .pin9(1'b1), .pin10(1'b1), .pin11(U2_pin11[3]), .pin12(U2_pin11[2]), .pin13(U2_pin11[1]),
    .pin14(U2_pin11[0]), .pin15(RCO), .pin16(1'b1));
  nand nand_5 (nand_5_out, Inc_nJp, Inc_nJp);
  xor xor_1 (xor_1_out, MOSI, PC_Din);
  Seven_Seg_Hex seven_seg_hex_11 (.d(U2_pin11), .dp(1'b0));
  nand nand_6 (nand_6_out, U2_pin11[3], U2_pin11[3]);
  nand nand_7 (SCLK, nand_6_out, GCLK);
  _74595 U13 (
    .pin1(U13_pin3[2]), .pin2(U13_pin3[1]), .pin3(U13_pin3[0]), .pin4(U13_pin7[3]), .pin5(U13_pin7[2]),
    .pin6(U13_pin7[1]), .pin7(U13_pin7[0]), .pin8(1'b0), .pin10(nRESET), .pin11(SCLK), .pin12(RCLK),
    .pin13(1'b0), .pin14(xor_1_out), .pin15(U13_pin3[3]), .pin16(1'b1));  // open: pin9
  xor xor_2 (TogglenSS, 1'b1, eq_42);
  nand nand_8 (nand_8_out, MOSI, nand_5_out);
  nand nand_9 (nand_9_out, Inc_nJp, Sum);
  nand nand_10 (PC_Din, nand_8_out, nand_9_out);
  _74595 U4 (
    .pin1(PC14), .pin2(PC13), .pin3(PC12), .pin4(PC11), .pin5(PC10), .pin6(PC9), .pin7(PC8), .pin8(1'b0),
    .pin9(SER), .pin10(nRESET), .pin11(GCLK), .pin12(RCLK), .pin13(1'b0), .pin14(PC_Din), .pin15(PC15),
    .pin16(1'b1));
  nand nand_11 (nand_11_out, U13_pin7[1], U13_pin3[2]);
  DiodeForward diodeforward_1 (.in(U13_pin3[3]), .out(eq_42));
  DiodeForward diodeforward_2 (.in(U13_pin3[1]), .out(eq_42));
  DiodeForward diodeforward_3 (.in(U13_pin3[0]), .out(eq_42));
  DiodeForward diodeforward_4 (.in(U13_pin7[3]), .out(eq_42));
  DiodeForward diodeforward_5 (.in(U13_pin7[2]), .out(eq_42));
  DiodeForward diodeforward_6 (.in(U13_pin7[0]), .out(eq_42));
  DiodeForward diodeforward_7 (.in(nand_11_out), .out(eq_42));
  PullDown pulldown_1 (.out(eq_42));
  nand nand_12 (nand_12_out, PC_Dout, PC_CIN);
  xor xor_3 (Sum, PC_Dout, PC_CIN);
  LED led_1 (.in(nSS));
  _74595 U5 (
    .pin1(PC6), .pin2(PC5), .pin3(PC4), .pin4(PC3), .pin5(PC2), .pin6(PC1), .pin7(PC0), .pin8(1'b0),
    .pin9(PC_Dout), .pin10(nRESET), .pin11(GCLK), .pin12(RCLK), .pin13(1'b0), .pin14(SER), .pin15(PC7),
    .pin16(1'b1));
  _7474 U9 (
    .pin1(1'b1), .pin2(U9_pin2), .pin3(TogglenSS), .pin4(nRESET), .pin5(nSS), .pin6(U9_pin2), .pin7(1'b0),
    .pin9(PC_CIN), .pin10(nLOADB), .pin11(GCLK), .pin12(PC_COUT), .pin13(1'b1), .pin14(1'b1));  // open: pin8
  _74175 U10 (
    .pin1(nRESET), .pin2(T17), .pin3(RCLK), .pin4(RCO), .pin5(T17), .pin6(nT18), .pin7(T18), .pin8(1'b0),
    .pin9(clk), .pin10(LD), .pin11(nLOADB), .pin12(RUN), .pin13(LD), .pin14(nT1), .pin15(T1), .pin16(1'b1));
  nand nand_13 (PC_COUT, nand_12_out, nand_12_out);
  Seven_Seg_Hex seven_seg_hex_12 (.d({A15, A14, A13, A12}), .dp(1'b0));
  Seven_Seg_Hex seven_seg_hex_13 (.d({A11, A10, A9, A8}), .dp(1'b0));
  _74595 U21 (
    .pin1(A14), .pin2(A13), .pin3(A12), .pin4(A11), .pin5(A10), .pin6(A9), .pin7(A8), .pin8(1'b0),
    .pin9(U21_pin9), .pin10(nCLR), .pin11(GCLK), .pin12(nTC), .pin13(nSEL), .pin14(RPC_DIN), .pin15(A15),
    .pin16(1'b1));
  _74595 U22 (
    .pin1(A6), .pin2(A5), .pin3(A4), .pin4(A3), .pin5(A2), .pin6(A1), .pin7(A0), .pin8(1'b0),
    .pin9(RPC_Dout), .pin10(nCLR), .pin11(GCLK), .pin12(nTC), .pin13(nSEL), .pin14(U21_pin9), .pin15(A7),
    .pin16(1'b1));
  _7474 U23 (
    .pin1(1'b1), .pin2(1'b1), .pin3(1'b1), .pin4(1'b1), .pin7(1'b0), .pin9(RPC_CIN), .pin10(nLOADB),
    .pin11(GCLK), .pin12(RPC_COUT), .pin13(1'b1), .pin14(1'b1));  // open: pin5, pin6, pin8
  Seven_Seg_Hex seven_seg_hex_14 (.d({A7, A6, A5, A4}), .dp(1'b0));
  Seven_Seg_Hex seven_seg_hex_15 (.d({A3, A2, A1, A0}), .dp(1'b0));
  nand nand_14 (nTC, TC, TC);
  Seven_Seg_Hex seven_seg_hex_16 (.d({BUS7, BUS6, BUS5, BUS4}), .dp(1'b0));
  Seven_Seg_Hex seven_seg_hex_17 (.d({BUS3, BUS2, BUS1, BUS0}), .dp(1'b0));
  _74165 U28 (
    .pin1(nTC), .pin2(GCLK), .pin3(BUS3), .pin4(BUS2), .pin5(BUS1), .pin6(BUS0), .pin8(1'b0), .pin9(MISO),
    .pin10(1'b0), .pin11(BUS7), .pin12(BUS6), .pin13(BUS5), .pin14(BUS4), .pin15(1'b0), .pin16(1'b1));  // open: pin7
  nand nand_15 (nand_15_out, Inc_nJump1, Inc_nJump1);
  nand nand_16 (nand_16_out, RPC_Dout, RPC_CIN);
  nand nand_17 (nand_17_out, RPC_Dout, RPC_CIN);
  // _28c256 U24: pin names not known; wires that end beside it: A14, A12, A7, A6, A5, A4, A3, A2, A1, A0, BUS0, BUS1, BUS2, 1'b0, 1'b1, in_10, A13, A8, A9, A11, in_11, A10, in_12, BUS7
  nand nand_18 (nand_18_out, MOSI, nand_15_out);
  nand nand_19 (nand_19_out, Inc_nJump1, nand_25_out);
  nand nand_20 (nand_20_out, RPC_Dout, nand_16_out);
  nand nand_21 (nand_21_out, nand_16_out, RPC_CIN);
  nand nand_22 (RPC_COUT, nand_17_out, nand_17_out);
  nand nand_23 (SEL, nSEL, nSEL);
  Reset reset_2 (.out(nCLR));
  _74161 U29 (
    .pin1(nCLR), .pin2(GCLK), .pin3(1'b0), .pin4(1'b0), .pin5(1'b0), .pin6(1'b0), .pin7(1'b1), .pin8(1'b0),
    .pin9(1'b1), .pin10(1'b1), .pin11(U29_pin14[3]), .pin12(U29_pin14[2]), .pin13(U29_pin14[1]),
    .pin14(U29_pin14[0]), .pin15(TC), .pin16(1'b1));
  nand nand_24 (RPC_DIN, nand_18_out, nand_19_out);
  nand nand_25 (nand_25_out, nand_20_out, nand_21_out);
  Seven_Seg_Hex seven_seg_hex_18 (.d(U29_pin14), .dp(1'b0));

  // Other names for the same wires on the sheet: IR0 = D0; IR1 = D1; IR2 = D2; IR3 = D3; IR4 = D4; IR5 = D5; IR6 = D6;
  //   IR7 = D7; nOERAM = in_11; nRAMCE = in_12; nT0 = nLOADB; nT17 = RCLK; nWERAM = in_10; PC_CLK = GCLK;
  //   RD0 = MISO_L[0]; RD1 = MISO_L[1]; RD2 = MISO_L[2]; RD3 = MISO_L[3]; RD4 = MISO_H[0]; RD5 = MISO_H[1];
  //   RD6 = MISO_H[2]; RD7 = MISO_H[3]; T0 = LD

  // Notes on the sheet:
  //   clk: Hz: 1000
  //   Inc_nJp: default 1
  //   Inc_nJump1: default 1
  //   in_10: default 1
  //   SPI Controller 01
  //   PC ADDRESS
  //   ROM
  //   STEP/RUN
  //   MOSI
  //   CLOCK SEQUENCER
  //   REGISTERS
  //   MISO
  //   U1
  //   8-bit OUTPUT REGISTER
  //   8-bit INPUT REGISTER
  //   XOR Instr
  //   U12
  //   PC Half-Adder
  //   U8
  //   "42"
  //   # Clock
  //   U11
  //   U12A
  //   $42 Detect
  //   D-FFs
  //   PC Carry FF
  //   SEQUENCER FFs
  //   PC
  //   SPI PROM
  //   ADDR_H  ADDR_L
  //   U27
  //   U25
  //   U26
endmodule
